# Fritzing sketch 10ldr_lux (saved by Fritzing 0.9.6b)
breadboards: 1

parts:
  Mod1 = Raspberry Pi Pico W
  LDR = Light Sensor

nets:
  N1: Mod1.pin_3, Mod1.pin_13, LDR.no_name_yet#connectorUARTVCC-0
  N2: Mod1.pin_31, LDR.no_name_yet#connectorUARTGND-0
  N3: Mod1.pin_36, LDR.no_name_yet#connectorRXD-1

custom parts:
  Raspberry Pi Pico W: Raspberry Pi Pico W. Based around the RP2040 microcontroller the Pico W is a low cost microcontroller device bringing Raspberry Pi quality, cost, and easy of use to the microcontroller space. The areas marked KEEPOUT in pcb silkscreen should not have traces running through them to avoid shorts on a soldered in module!
